# Fritzing sketch Fritzing_BreadboardFile (saved by Fritzing 0.9.3b)
breadboards: 1

parts:
  ESP32_SLAVE = ESP32S-HiLetgo [part_number=ESP32S-HiLetgo]
  ESP32_MASTER = ESP32S-HiLetgo [part_number=ESP32S-HiLetgo]
  MEGA2560_REV3_SLAVE = Arduino Mega 2560 (Rev3)
  Micro_USB = Micro USB B Plug
  Micro_USB_2 = USB A Plug
  Micro_USB_3 = USB A Plug
  Micro_USB_4 = Micro USB B Plug
  USB_A = Micro USB B Plug
  USB_A_2 = Micro USB B Plug
  USB_A_3 = USB A Plug
  UNO_REV3_SLAVE = Arduino Uno (Rev3)
  USBA = USB A Plug
  Power_Supply = YwRobot Breadboard Power Supply [part_number=545043]
  Liquid_Display_2x16 = LCD-16X2 [package=lcd-16x2]
  R1 = Trimmer Potentiometer [maximum_resistance=10kΩ package=THT]
  J2 = TFT_LCD 480X320 HiLetgo
  J3 = Generic male header - 18 pins [form="♂ (male)" package=THT]  # not connected

nets:
  GND: ESP32_SLAVE.GND, ESP32_MASTER.GND, MEGA2560_REV3_SLAVE.GND, UNO_REV3_SLAVE.GND, J2.GND#17
  5V: ESP32_SLAVE.VIN, ESP32_MASTER.VIN, MEGA2560_REV3_SLAVE.5V, UNO_REV3_SLAVE.5V, J2.5v, J2.5V
  N1: ESP32_SLAVE.GPIO21, ESP32_MASTER.GPIO21, MEGA2560_REV3_SLAVE.D20/SDA, MEGA2560_REV3_SLAVE.SDA
  N2: ESP32_SLAVE.GPIO22, ESP32_MASTER.GPIO22, MEGA2560_REV3_SLAVE.D21/SCL, UNO_REV3_SLAVE.A5/SCL
  N3: MEGA2560_REV3_SLAVE.D50, J2.CS
  N4: MEGA2560_REV3_SLAVE.D51, J2.RST
  N5: MEGA2560_REV3_SLAVE.D52, J2.MISO
  N6: Micro_USB.usb, Micro_USB_2.usb
  N7: Micro_USB_3.usb, Micro_USB_4.usb
  N8: USB_A.usb, USBA.usb
  N9: USB_A_2.usb, USB_A_3.usb
  N10: UNO_REV3_SLAVE.D11_PWM/MOSI, Liquid_Display_2x16.E
  N11: UNO_REV3_SLAVE.D12/MISO, Liquid_Display_2x16.RS
  N12: UNO_REV3_SLAVE.D2, Liquid_Display_2x16.DB7
  N13: UNO_REV3_SLAVE.D3_PWM, Liquid_Display_2x16.DB6
  N14: UNO_REV3_SLAVE.D4, Liquid_Display_2x16.DB5
  N15: UNO_REV3_SLAVE.D5_PWM, Liquid_Display_2x16.DB4
  N16: Power_Supply.VCC#5, Power_Supply.VCC#6, Liquid_Display_2x16.VDD, Liquid_Display_2x16.A, R1.leg2
  GND_2: Power_Supply.GND, Liquid_Display_2x16.VSS, Liquid_Display_2x16.R_W, Liquid_Display_2x16.K, R1.leg1
  N17: Liquid_Display_2x16.VO, R1.wiper

custom parts:
  ESP32S-HiLetgo: HiLetgo ESP-WROOM-32 ESP32 ESP-32S Development Board 2.4GHz Dual-Mode WiFi + Bluetooth Dual Cores Microcontroller The ESP32 integrated with Antenna switches, RF Balun, power amplifiers, low-noise amplifiers, filters, and management modules, and the entire solution occupies the least area of PCB. 2.4 GHz Wi-Fi plus Bluetooth dual-mode chip, with TSMC Ultra-low power consumption 40nm technology,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
  YwRobot Breadboard Power Supply: The YwRobot Breadboard Power Supply (MB-V2) has two power rails; they can be 5V or 3V3. Power to the module can be provided through the female USB socket or through the A10 (female) 2.1mm power jack.
  TFT_LCD 480X320 HiLetgo: The HiLetgo 3.5" TFT LCD Display is a touch screen with a resolution of 480x320 pixels, utilizing the ILI9486 or ILI9488 controllers. This type of display is compatible with microcontrollers such as the Arduino Mega2560 and features 36 pins for connection.
  Generic male header - 18 pins: Generic male header
